# Fritzing sketch garage-cerberus (saved by Fritzing 0.9.3b)

parts:
  U1 = NodeMCU V1.0
  UV_LASER = Super Flux LED blue [color=Blue]
  J1 = Piezo Speaker
  R1 = PHOTOCELL [package=photocell]
  R2 = Resistor [tolerance=±5% resistance=10k package="0603 [SMD]"]

nets:
  N1: U1.D2, R1.P$2, R2.Pin_1
  N2: U1.3V3, R1.P$1
  N3: U1.GND, UV_LASER.cathode, J1.pin1, R2.Pin_0
  N4: U1.D8, J1.pin2
  N5: U1.RSV, UV_LASER.anode

custom parts:
  NodeMCU V1.0: ESP8266 based NodeMCU
